# Fritzing sketch fritzing_dualreg_example (saved by Fritzing 0.9.3b)
breadboards: 1

parts:
  Часть1 = Arduino Micro (Rev3)
  Q1 = NPN-Transistor [package="TO92 [THT]"]
  Q2 = PNP-Transistor [package="TO92 [THT]"]
  Q3 = PNP-Transistor [package="TO92 [THT]"]
  Q4 = NPN-Transistor [package="TO92 [THT]"]
  M1 = DC Motor
  R1 = Resistor [tolerance=±5% resistance=1k package=THT]
  R2 = Resistor [tolerance=±5% resistance=1k package=THT]
  R4 = Resistor [tolerance=±5% resistance=1k package=THT]
  R3 = Resistor [tolerance=±5% resistance=1k package=THT]
  U1 = Voltage Regulator - 5V [package="TO220 [THT]"]
  C1 = Electrolytic Capacitor [capacitance=1mF package="100 mil [THT, electrolytic]"]
  Q5 = NPN-Transistor [package="TO92 [THT]"]
  Q6 = NPN-Transistor [package="TO92 [THT]"]
  R5 = Resistor [tolerance=±5% resistance=1k package=THT]
  R6 = Resistor [tolerance=±5% resistance=1k package=THT]
  J1 = Dagu DGServo 9g header connector (female) [package=THT]
  Q7 = NPN-Transistor [package="TO92 [THT]"]
  Q8 = PNP-Transistor [package="TO92 [THT]"]
  Q9 = PNP-Transistor [package="TO92 [THT]"]
  Q10 = NPN-Transistor [package="TO92 [THT]"]
  M2 = DC Motor
  R7 = Resistor [tolerance=±5% resistance=1k package=THT]
  R8 = Resistor [tolerance=±5% resistance=1k package=THT]
  R9 = Resistor [tolerance=±5% resistance=1k package=THT]
  R10 = Resistor [tolerance=±5% resistance=1k package=THT]
  Q11 = NPN-Transistor [package="TO92 [THT]"]
  Q12 = NPN-Transistor [package="TO92 [THT]"]
  R11 = Resistor [tolerance=±5% resistance=1k package=THT]
  R12 = Resistor [tolerance=±5% resistance=1k package=THT]
  J2 = Dagu DGServo 9g header connector (female) [package=THT]

nets:
  GND: Часть1.GND, Q1.E, Q4.E, U1.GND, C1.-, Q5.E, Q6.E, J1.gnd, Q7.E, Q10.E, Q11.E, Q12.E, J2.gnd
  N1: Часть1.D5_PWM, R3.Pin_1, R5.Pin_1
  N2: Часть1.D6_PWM/A7, J1.pulse
  N3: Часть1.D7, J2.pulse
  N4: Часть1.D9_PWM/A9, R4.Pin_1, R6.Pin_1
  N5: Часть1.D10_PWM/A10, R10.Pin_1, R11.Pin_1
  N6: Часть1.D11_PWM, R9.Pin_1, R12.Pin_1
  N7: Часть1.VIN, Q2.E, Q3.E, U1.input_voltage, Q8.E, Q9.E
  VCC: Часть1.5V, U1.output_voltage, C1.+, J1.Vcc, J2.Vcc
  N8: Q1.B, R3.Pin_0
  N9: Q1.C, Q2.C, M1.pin_2
  N10: Q2.B, R1.Pin_1
  N11: Q3.B, R2.Pin_0
  N12: Q3.C, Q4.C, M1.pin_1
  N13: Q4.B, R4.Pin_0
  N14: R1.Pin_0, Q5.C
  N15: R2.Pin_1, Q6.C
  N16: Q5.B, R6.Pin_0
  N17: Q6.B, R5.Pin_0
  N18: Q7.B, R10.Pin_0
  N19: Q7.C, Q8.C, M2.pin_2
  N20: Q8.B, R7.Pin_1
  N21: Q9.B, R8.Pin_0
  N22: Q10.B, R9.Pin_0
  N23: R7.Pin_0, Q11.C
  N24: R8.Pin_1, Q12.C
  N25: Q11.B, R12.Pin_0
  N26: Q12.B, R11.Pin_0
